// Logisim project sram8bit.circ as structural Verilog: 1 circuit, main circuit main
module main (
  input  BFS,
  input  BFS_2,
  input  BFS_3,
  input  in_4,
  input  in_5,
  input  in_6,
  input  in_7,
  input  in_8,
  input  in_9,
  input  in_10,
  input  in_11,
  output out_12,
  output out_13,
  output out_14,
  output out_15,
  output out_16,
  output out_17,
  output out_18,
  output out_19,
  output out_20,
  output out_21,
  output out_22,
  output out_23,
  output out_24,
  output out_25,
  output out_26,
  output out_27
);

  wire and_1_out, and_2_out, and_3_out, and_4_out, and_5_out, and_6_out, and_7_out, and_8_out, and_9_out,
       and_10_out, and_11_out, and_12_out, and_13_out, and_14_out, and_15_out, and_16_out, and_17_out,
       and_18_out, and_19_out, and_20_out, and_21_out, and_22_out, and_23_out, and_24_out, and_25_out,
       and_26_out, and_27_out, and_28_out, and_29_out, and_30_out, and_31_out, and_32_out, and_33_out,
       and_34_out, and_35_out, and_36_out, and_37_out, and_38_out, and_39_out, and_40_out, and_41_out,
       and_42_out, and_43_out, and_44_out, and_45_out, and_46_out, and_47_out, and_48_out, not_1_out,
       not_2_out, not_3_out, not_4_out, not_5_out, not_6_out, not_7_out, not_8_out, not_9_out, not_10_out,
       not_11_out, not_12_out, not_13_out, not_14_out, not_15_out, not_16_out, not_17_out, not_18_out,
       not_19_out, not_20_out, not_21_out, not_22_out, not_23_out, not_24_out, not_25_out, not_26_out,
       not_27_out, not_28_out, not_29_out, not_30_out, not_31_out, not_32_out, or_1_out, or_2_out, or_3_out,
       or_4_out, or_5_out, or_6_out, or_7_out, or_8_out, or_9_out, or_10_out, or_11_out, or_12_out,
       or_13_out, or_14_out, or_15_out, or_16_out;

  and and_1 (and_1_out, BFS_3, BFS);
  and and_2 (and_2_out, BFS_3, BFS);
  and and_3 (and_3_out, BFS_3, BFS);
  and and_4 (and_4_out, BFS_3, BFS);
  and and_5 (and_5_out, BFS_3, BFS);
  and and_6 (and_6_out, BFS_3, BFS);
  and and_7 (and_7_out, BFS_3, BFS);
  and and_8 (and_8_out, BFS_3, BFS);
  and and_9 (and_9_out, BFS_2, BFS);
  and and_10 (and_10_out, BFS_2, BFS);
  and and_11 (and_11_out, BFS_2, BFS);
  and and_12 (and_12_out, BFS_2, BFS);
  and and_13 (and_13_out, BFS_2, BFS);
  and and_14 (and_14_out, BFS_2, BFS);
  and and_15 (and_15_out, BFS_2, BFS);
  and and_16 (and_16_out, BFS_2, BFS);
  not not_1 (not_1_out, in_11);
  not not_2 (not_2_out, in_10);
  not not_3 (not_3_out, in_9);
  not not_4 (not_4_out, in_8);
  not not_5 (not_5_out, in_7);
  not not_6 (not_6_out, in_6);
  not not_7 (not_7_out, in_5);
  not not_8 (not_8_out, in_4);
  not not_9 (not_9_out, in_11);
  not not_10 (not_10_out, in_10);
  not not_11 (not_11_out, in_9);
  not not_12 (not_12_out, in_8);
  not not_13 (not_13_out, in_7);
  not not_14 (not_14_out, in_6);
  not not_15 (not_15_out, in_5);
  not not_16 (not_16_out, in_4);
  and and_17 (and_17_out, in_11, and_1_out);
  and and_18 (and_18_out, and_1_out, not_1_out);
  and and_19 (and_19_out, in_10, and_2_out);
  and and_20 (and_20_out, and_2_out, not_2_out);
  and and_21 (and_21_out, in_9, and_3_out);
  and and_22 (and_22_out, and_3_out, not_3_out);
  and and_23 (and_23_out, in_8, and_4_out);
  and and_24 (and_24_out, and_4_out, not_4_out);
  and and_25 (and_25_out, in_7, and_5_out);
  and and_26 (and_26_out, and_5_out, not_5_out);
  and and_27 (and_27_out, in_6, and_6_out);
  and and_28 (and_28_out, and_6_out, not_6_out);
  and and_29 (and_29_out, in_5, and_7_out);
  and and_30 (and_30_out, and_7_out, not_7_out);
  and and_31 (and_31_out, in_4, and_8_out);
  and and_32 (and_32_out, and_8_out, not_8_out);
  and and_33 (and_33_out, in_11, and_9_out);
  and and_34 (and_34_out, and_9_out, not_9_out);
  and and_35 (and_35_out, in_10, and_10_out);
  and and_36 (and_36_out, and_10_out, not_10_out);
  and and_37 (and_37_out, in_9, and_11_out);
  and and_38 (and_38_out, and_11_out, not_11_out);
  and and_39 (and_39_out, in_8, and_12_out);
  and and_40 (and_40_out, and_12_out, not_12_out);
  and and_41 (and_41_out, in_7, and_13_out);
  and and_42 (and_42_out, and_13_out, not_13_out);
  and and_43 (and_43_out, in_6, and_14_out);
  and and_44 (and_44_out, and_14_out, not_14_out);
  and and_45 (and_45_out, in_5, and_15_out);
  and and_46 (and_46_out, and_15_out, not_15_out);
  and and_47 (and_47_out, in_4, and_16_out);
  and and_48 (and_48_out, and_16_out, not_16_out);
  or or_1 (or_1_out, out_12, and_17_out);
  not not_17 (not_17_out, and_18_out);
  or or_2 (or_2_out, out_13, and_19_out);
  not not_18 (not_18_out, and_20_out);
  or or_3 (or_3_out, out_14, and_21_out);
  not not_19 (not_19_out, and_22_out);
  or or_4 (or_4_out, out_15, and_23_out);
  not not_20 (not_20_out, and_24_out);
  or or_5 (or_5_out, out_16, and_25_out);
  not not_21 (not_21_out, and_26_out);
  or or_6 (or_6_out, out_17, and_27_out);
  not not_22 (not_22_out, and_28_out);
  or or_7 (or_7_out, out_18, and_29_out);
  not not_23 (not_23_out, and_30_out);
  or or_8 (or_8_out, out_19, and_31_out);
  not not_24 (not_24_out, and_32_out);
  or or_9 (or_9_out, out_20, and_33_out);
  not not_25 (not_25_out, and_34_out);
  or or_10 (or_10_out, out_21, and_35_out);
  not not_26 (not_26_out, and_36_out);
  or or_11 (or_11_out, out_22, and_37_out);
  not not_27 (not_27_out, and_38_out);
  or or_12 (or_12_out, out_23, and_39_out);
  not not_28 (not_28_out, and_40_out);
  or or_13 (or_13_out, out_24, and_41_out);
  not not_29 (not_29_out, and_42_out);
  or or_14 (or_14_out, out_25, and_43_out);
  not not_30 (not_30_out, and_44_out);
  or or_15 (or_15_out, out_26, and_45_out);
  not not_31 (not_31_out, and_46_out);
  or or_16 (or_16_out, out_27, and_47_out);
  not not_32 (not_32_out, and_48_out);
  and and_49 (out_12, or_1_out, not_17_out);
  and and_50 (out_13, or_2_out, not_18_out);
  and and_51 (out_14, or_3_out, not_19_out);
  and and_52 (out_15, or_4_out, not_20_out);
  and and_53 (out_16, or_5_out, not_21_out);
  and and_54 (out_17, or_6_out, not_22_out);
  and and_55 (out_18, or_7_out, not_23_out);
  and and_56 (out_19, or_8_out, not_24_out);
  and and_57 (out_20, or_9_out, not_25_out);
  and and_58 (out_21, or_10_out, not_26_out);
  and and_59 (out_22, or_11_out, not_27_out);
  and and_60 (out_23, or_12_out, not_28_out);
  and and_61 (out_24, or_13_out, not_29_out);
  and and_62 (out_25, or_14_out, not_30_out);
  and and_63 (out_26, or_15_out, not_31_out);
  and and_64 (out_27, or_16_out, not_32_out);

  // Notes on the sheet:
  //   and the memory selection
  //   I'm going to need some buffers for the clock 
  //   a single input cannot power 200 other gates
  //   clock
  //   memory sel
  //   1
  //   0
  //   data bus
  //   1  2  4  8  16 32 64 128
  //   WRITER
  //   WRITER
endmodule
